# Fritzing sketch 3d Scanner (saved by Fritzing 1.0.1rc)
breadboards: 1

parts:
  U1 = LCD-16X2 [package=lcd-16x2]
  Part1 = Arduino Uno (Rev3) - ICSP
  Part2 = Thumb Joystick
  M1 = Dagu DGServo 9g (Pan and tilt) [part_number=RS001B]
  SM1 = 28BYJ-48 Stepper Motor [part_number=28BYJ-48]  # not connected
  Driver1 = 28BYJ-48 Driver Module [part_number=ULN2003 package=THT]
  LCM1602_IIC1 = LCM1602 IIC [part_number="LCM1602 IIC" chip_label="LCM1602 IIC" package="DIP (Dual Inline) [THT]"]

nets:
  VSS: U1.VSS, LCM1602_IIC1.VSS
  VDD: U1.VDD, LCM1602_IIC1.VDD
  N1: U1.VO, LCM1602_IIC1.V0
  N2: U1.RS, LCM1602_IIC1.RS
  N3: U1.R_W, LCM1602_IIC1.RW
  N4: U1.E, LCM1602_IIC1.E
  N5: U1.DB0, LCM1602_IIC1.D0
  N6: U1.DB1, LCM1602_IIC1.D1
  N7: U1.DB2, LCM1602_IIC1.D2
  N8: U1.DB3, LCM1602_IIC1.D3
  N9: U1.DB4, LCM1602_IIC1.D4
  N10: U1.DB5, LCM1602_IIC1.D5
  N11: U1.DB6, LCM1602_IIC1.D6
  N12: U1.DB7, LCM1602_IIC1.D7
  N13: U1.A, LCM1602_IIC1.A
  N14: U1.K, LCM1602_IIC1.K
  N15: Part1.A0, Part2.HORZ
  N16: Part1.A1, Part2.VERT
  N17: Part1.A4/SDA, LCM1602_IIC1.SDA
  N18: Part1.A5/SCL, LCM1602_IIC1.SCL
  N19: Part1.ICSP_MISO, Part1.D12/MISO, Driver1.IN4
  N20: Part1.D9_PWM, Driver1.IN1
  N21: Part1.D10_PWM/SS, Driver1.IN2
  N22: Part1.D11_PWM/MOSI, Driver1.IN3
  GND: Part1.GND, Part2.GND, M1.gnd, Driver1.GND, LCM1602_IIC1.GND
  N23: Part1.D2, Part2.SEL
  N24: Part1.D3_PWM, M1.pulse
  N25: Part1.RESET, M1.vcc
  N26: Part1.5V, Driver1.Vmotor
  VCC: Part1.VIN, Part2.VCC, LCM1602_IIC1.VCC
  N27: LCM1602_IIC1.LED_A, LCM1602_IIC1.LED_B

custom parts:
  28BYJ-48 Stepper Motor: Unipolar Stepper Motor 28BYJ-48 Top coil - pink & orange Bottom coil - blue & yellow Common rail - red Connector pins: blue - pink - yellow - orange - red
  28BYJ-48 Driver Module: Generic male header
  LCM1602 IIC: I2C-Module to use a 1602 or 2004 LCD on with the wire.h libory Serial LCD Modul
